// Logisim project 4bitadder.circ as structural Verilog: 2 circuits, main circuit adder1
module main (
  input  a,
  input  b,
  input  Cin,
  output S,
  output Cout
);

  wire and_1_out, and_2_out, xor_1_out;

  xor xor_1 (xor_1_out, a, b);
  xor xor_2 (S, xor_1_out, Cin);
  and and_1 (and_1_out, Cin, xor_1_out);
  and and_2 (and_2_out, b, a);
  or or_1 (Cout, and_1_out, and_2_out);
endmodule

module adder1 (
  input  A0,
  input  B0,
  input  cin,
  input  A1,
  input  B1,
  input  A2,
  input  B2,
  input  A3,
  input  B3,
  output S0,
  output S1,
  output S2,
  output S3,
  output cout
);

  wire main_1_cout, main_2_cout, main_3_cout;

  main main_1 (.a(A0), .b(B0), .Cin(cin), .S(S0), .Cout(main_1_cout));
  main main_2 (.a(A1), .b(B1), .Cin(main_1_cout), .S(S1), .Cout(main_2_cout));
  main main_3 (.a(A2), .b(B2), .Cin(main_2_cout), .S(S2), .Cout(main_3_cout));
  main main_4 (.a(A3), .b(B3), .Cin(main_3_cout), .S(S3), .Cout(cout));
endmodule
